# Fritzing sketch bidirectional-motor (saved by Fritzing 0.9.0b)
breadboards: 1

parts:
  Part1 = Spark Core (v1.0)
  D1 = Rectifier Diode [part_number=1N4001 package="Melf DO-213 AB [SMD]"]
  D2 = Rectifier Diode [part_number=1N4001 package="Melf DO-213 AB [SMD]"]
  M1 = DC Motor
  M2 = DC Motor
  VCC1 = 4 x AAA Battery Mount
  IC1 = L293D [package=THT]
  D3 = Rectifier Diode [part_number=1N4001 package="Melf DO-213 AB [SMD]"]  # not connected

nets:
  N1: Part1.A0, IC1.Enable_1
  N2: Part1.A4, IC1.Enable_2
  N3: Part1.GND, VCC1.-, IC1.0V
  N4: Part1.VIN, D1.cathode, D2.cathode, VCC1.+, IC1.+Vmotor, IC1.+V
  N5: Part1.D2, IC1.In_4
  N6: Part1.D3, IC1.In_3
  N7: Part1.D4, IC1.In_2
  N8: Part1.D6, IC1.In_1
  N9: D1.anode, M2.pin_2, IC1.Out_4_(_Controlled_by_Enable_2_)
  N10: D2.anode, M2.pin_1, IC1.Out_3_(_Controlled_by_Enable_2_)
  N11: M1.pin_1, IC1.Out_2_(_Controlled_by_Enable_1_)
  N12: M1.pin_2, IC1.Out_1_(_Controlled_by_Enable_1_)
